# Fritzing sketch Ligação Servo (saved by Fritzing 0.9.3b)

parts:
  Componente1 = Arduino Uno (Rev3)
  J1 = Basic Servo

nets:
  N1: Componente1.D3_PWM, J1.pulse
  5V: Componente1.5V, J1.vcc
  GND: Componente1.GND, J1.gnd
