# Fritzing sketch projeto final (saved by Fritzing 0.9.3b)
breadboards: 1

parts:
  Componente1 = Arduino Uno (Rev3)
  Componente2 = Thumb Joystick
  Componente3 = Thumb Joystick
  J1 = Basic Servo
  J2 = Basic Servo
  J3 = Basic Servo
  J4 = Basic Servo

nets:
  N1: Componente1.A0, Componente2.VERT
  N2: Componente1.A1, Componente2.HORZ
  N3: Componente1.A2, Componente3.VERT
  N4: Componente1.A3, Componente3.HORZ
  N5: Componente1.D9_PWM, J4.pulse
  N6: Componente1.D3_PWM, J3.pulse
  N7: Componente1.D5_PWM, J2.pulse
  N8: Componente1.D6_PWM, J1.pulse
  VCC: Componente1.5V, Componente2.VCC, Componente3.VCC, J1.vcc, J2.vcc, J3.vcc, J4.vcc
  GND: Componente1.GND, Componente2.GND, Componente3.GND, J1.gnd, J2.gnd, J3.gnd, J4.gnd
